# Fritzing sketch DHT (saved by Fritzing 0.9.4)
breadboards: 1

parts:
  RHT1 = Humidity and Temperature Sensor RHT03
  Part1 = Arduino Uno (Rev3)
  LED1 = LED - 5mm [color="Red (633nm)" package="5 mm [THT]"]
  LED2 = LED - 5mm [color="Red (633nm)" package="5 mm [THT]"]
  R1 = Resistor [tolerance=±5% resistance=220 package=THT]

nets:
  VCC: RHT1.Vcc, Part1.5V
  N1: RHT1.Data-signal, Part1.D8, R1.Pin_1
  N2: RHT1.GND_2, Part1.GND, LED1.cathode, LED2.cathode, R1.Pin_0
  N3: Part1.D2, LED1.anode
  N4: Part1.D4, LED2.anode
