# Fritzing sketch sevensegment (saved by Fritzing 0.9.4)
breadboards: 1

parts:
  7_Segment1 = 7 Segment Display
  R1 = Resistor [tolerance=±5% resistance=220 package=THT]
  R2 = Resistor [tolerance=±5% resistance=220 package=THT]
  R3 = Resistor [tolerance=±5% resistance=220 package=THT]
  R4 = Resistor [tolerance=±5% resistance=220 package=THT]
  R5 = Resistor [tolerance=±5% resistance=220 package=THT]
  R6 = Resistor [tolerance=±5% resistance=220 package=THT]
  R7 = Resistor [tolerance=±5% resistance=220 package=THT]
  Part1 = Arduino Uno (Rev3)

nets:
  N1: 7_Segment1.Segment_G, 7_Segment1.Segment_A, R1.Pin_0, R3.Pin_0, R6.Pin_0
  N2: 7_Segment1.Segment_F, 7_Segment1.Segment_B, R4.Pin_0
  N3: 7_Segment1.Segment_E, 7_Segment1.Segment_C, R5.Pin_1, R7.Pin_1
  N4: 7_Segment1.Segment_D, 7_Segment1.Segment_DP, R2.Pin_1
  N5: R1.Pin_1, Part1.D4
  N6: R2.Pin_0, Part1.D7
  N7: R4.Pin_1, Part1.D3_PWM
  N8: R5.Pin_0, Part1.D6_PWM
  N9: R6.Pin_1, Part1.D2
  N10: R7.Pin_0, Part1.D5_PWM
